# Fritzing sketch Sbot Circuit (saved by Fritzing 0.9.4)

parts:
  Part1 = NANO 33 BLE
  DC_Mot_Enc1 = DC Motor with two-phase hall-encoder [part_number=VT-E-G25A-06-177E]
  DC_Mot_Enc2 = DC Motor with two-phase hall-encoder [part_number=VT-E-G25A-06-177E]
  Part2 = Motor Driver 1A Dual TB6612FNG
  Part3 = JeePlug experimenter's board

nets:
  GND: Part1.GND, DC_Mot_Enc1.pin6, DC_Mot_Enc2.pin6, Part2.GND, Part3.N$18
  N1: Part1.D4, Part2.PWMA
  N2: Part1.D5~, Part2.AIN2
  N3: Part1.D6~, Part2.AIN1
  N4: Part1.D7, Part2.STBY
  N5: Part1.D8, Part2.BIN1
  N6: Part1.D9~, Part2.BIN2
  N7: Part1.D10~, Part2.PWMB
  N8: Part1.+5V, DC_Mot_Enc1.pin3, DC_Mot_Enc2.pin3, Part3.N$14
  N9: Part1.A6, DC_Mot_Enc2.pin4
  N10: Part1.A5, DC_Mot_Enc2.pin5
  N11: Part1.A4, DC_Mot_Enc1.pin4
  N12: Part1.A3, DC_Mot_Enc1.pin5
  N13: DC_Mot_Enc1.pin1, Part2.B01
  N14: DC_Mot_Enc1.pin2, Part2.B02
  N15: DC_Mot_Enc2.pin1, Part2.A02
  N16: DC_Mot_Enc2.pin2, Part2.A01

custom parts:
  NANO 33 BLE: This compact and reliable Nano board is built around the NINA B306 module, based on Nordic nRF 52840 and containing a powerful Cortex M4F. Its architecture, fully compatible with Arduino IDE Online and Offline, has a 9 axis Inertial Measurement Unit (IMU) and a reduced power consumption compared to other same size boards. This allows the design of wearable devices and movement sensing projects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
